// Logisim project ASKHSH1_2.circ as structural Verilog: 1 circuit, main circuit main
module main (
  input  in_1,
  input  in_2,
  input  in_3,
  input  in_4,
  output out_5
);

  wire n7402_1_pin1, n7402_1_pin4, n7402_1_pin7, n7402_1_pin10, n7402_1_pin12, n7402_1_pin14;

  _7402 #(.ShowInternalStructure("true"), .VccGndPorts("true")) u_7402_1 (
    .pin1(n7402_1_pin1), .pin2(in_1), .pin3(in_3), .pin4(n7402_1_pin4), .pin5(in_2), .pin6(in_3),
    .pin7(n7402_1_pin7), .pin14(n7402_1_pin14), .pin13(out_5), .pin12(n7402_1_pin12), .pin11(n7402_1_pin12),
    .pin10(n7402_1_pin10), .pin9(in_4), .pin8(in_2));
  _7427 #(.ShowInternalStructure("true"), .VccGndPorts("true")) u_7427_1 (
    .pin3(n7402_1_pin10), .pin4(n7402_1_pin4), .pin5(n7402_1_pin1), .pin6(n7402_1_pin12),
    .pin7(n7402_1_pin7), .pin14(n7402_1_pin14));  // open: pin1, pin2, pin13, pin12, pin11, pin10, pin9, pin8
  LED led_1 (.in(out_5));
  // also tied to GND on the sheet: n7402_1_pin7
  // also tied to VCC on the sheet: n7402_1_pin14
endmodule
