// Logisim project SCREENSHOT1_ASKHSH1.circ as structural Verilog: 1 circuit, main circuit main
module main (
  input  in_1,
  input  in_2,
  output out_3,
  output out_4,
  output out_5,
  output out_6,
  output out_7,
  output out_8
);

  wire n7404_1_pin7, n7404_1_pin14;

  _7404 #(.ShowInternalStructure("true"), .VccGndPorts("true")) u_7404_1 (
    .pin1(in_1), .pin2(out_4), .pin7(n7404_1_pin7), .pin14(n7404_1_pin14));  // open: pin3, pin4, pin5, pin6, pin13, pin12, pin11, pin10, pin9, pin8
  LED led_1 (.in(out_4));
  _7400 #(.ShowInternalStructure("true"), .VccGndPorts("true")) u_7400_1 (
    .pin1(in_1), .pin2(in_2), .pin3(out_5), .pin7(n7404_1_pin7), .pin14(n7404_1_pin14));  // open: pin4, pin5, pin6, pin13, pin12, pin11, pin10, pin9, pin8
  LED led_2 (.in(out_5));
  _7402 #(.ShowInternalStructure("true"), .VccGndPorts("true")) u_7402_1 (
    .pin1(out_6), .pin2(in_2), .pin3(in_1), .pin7(n7404_1_pin7), .pin14(n7404_1_pin14));  // open: pin4, pin5, pin6, pin13, pin12, pin11, pin10, pin9, pin8
  LED led_3 (.in(out_6));
  _7408 #(.ShowInternalStructure("true"), .VccGndPorts("true")) u_7408_1 (
    .pin1(in_1), .pin2(in_2), .pin3(out_7), .pin7(n7404_1_pin7), .pin14(n7404_1_pin14));  // open: pin4, pin5, pin6, pin13, pin12, pin11, pin10, pin9, pin8
  LED led_4 (.in(out_7));
  _7432 #(.ShowInternalStructure("true"), .VccGndPorts("true")) u_7432_1 (
    .pin1(in_1), .pin2(in_2), .pin3(out_8), .pin7(n7404_1_pin7), .pin14(n7404_1_pin14));  // open: pin4, pin5, pin6, pin13, pin12, pin11, pin10, pin9, pin8
  LED led_5 (.in(out_8));
  _7486 #(.ShowInternalStructure("true"), .VccGndPorts("true")) u_7486_1 (
    .pin1(in_1), .pin2(in_2), .pin3(out_3), .pin7(n7404_1_pin7), .pin14(n7404_1_pin14));  // open: pin4, pin5, pin6, pin13, pin12, pin11, pin10, pin9, pin8
  LED led_6 (.in(out_3));
  // also tied to GND on the sheet: n7404_1_pin7
  // also tied to VCC on the sheet: n7404_1_pin14
endmodule
