// Logisim project ASKHSH3.circ as structural Verilog: 1 circuit, main circuit main
module main (
  input  in_1,
  input  in_2,
  input  in_3,
  input  in_4,
  output out_5,
  output out_6,
  output out_7,
  output out_8
);

  wire n7404_1_pin2, n7404_1_pin4, n7404_1_pin7, n7404_1_pin14, n7408_1_pin3, n7408_1_pin6, n7408_1_pin11,
       n7486_1_pin11;

  _7404 #(.ShowInternalStructure("true"), .VccGndPorts("true")) u_7404_1 (
    .pin1(in_3), .pin2(n7404_1_pin2), .pin3(in_4), .pin4(n7404_1_pin4), .pin7(n7404_1_pin7),
    .pin14(n7404_1_pin14));  // open: pin5, pin6, pin13, pin12, pin11, pin10, pin9, pin8
  _7408 #(.ShowInternalStructure("true"), .VccGndPorts("true")) u_7408_1 (
    .pin1(n7404_1_pin2), .pin2(n7404_1_pin4), .pin3(n7408_1_pin3), .pin4(n7408_1_pin3), .pin5(in_2),
    .pin6(n7408_1_pin6), .pin7(n7404_1_pin7), .pin14(n7404_1_pin14), .pin13(in_4), .pin12(in_1),
    .pin11(n7408_1_pin11));  // open: pin10, pin9, pin8
  _7486 #(.ShowInternalStructure("true"), .VccGndPorts("true")) u_7486_1 (
    .pin1(n7408_1_pin11), .pin2(in_3), .pin3(out_7), .pin7(n7404_1_pin7), .pin14(n7404_1_pin14),
    .pin13(in_2), .pin12(in_1), .pin11(n7486_1_pin11));  // open: pin4, pin5, pin6, pin10, pin9, pin8
  _7432 #(.ShowInternalStructure("true"), .VccGndPorts("true")) u_7432_1 (
    .pin1(n7486_1_pin11), .pin2(n7408_1_pin6), .pin3(out_6), .pin7(n7404_1_pin7), .pin14(n7404_1_pin14));  // open: pin4, pin5, pin6, pin13, pin12, pin11, pin10, pin9, pin8

  assign out_5 = in_1;
  assign out_8 = in_4;
  // also tied to GND on the sheet: n7404_1_pin7
  // also tied to VCC on the sheet: n7404_1_pin14
endmodule
