// Logisim project askhsh1.circ as structural Verilog: 1 circuit, main circuit main
module main (
  input  CLEAR,
  input  set1,
  input  in_3
);

  wire CLK_out, n7474_1_pin5, n7474_1_pin7, n7474_1_pin9, n7474_1_pin10, n7474_1_pin14, n7474_2_pin5,
       n7474_2_pin9;

  Clock CLK (.out(CLK_out));
  _7474 #(.ShowInternalStructure("true"), .VccGndPorts("true")) u_7474_1 (
    .pin1(CLEAR), .pin2(in_3), .pin3(CLK_out), .pin4(set1), .pin5(n7474_1_pin5), .pin7(n7474_1_pin7),
    .pin14(n7474_1_pin14), .pin13(CLEAR), .pin12(n7474_1_pin5), .pin11(CLK_out), .pin10(n7474_1_pin10),
    .pin9(n7474_1_pin9));  // open: pin6, pin8
  _7474 #(.ShowInternalStructure("true"), .VccGndPorts("true")) u_7474_2 (
    .pin1(CLEAR), .pin2(n7474_1_pin9), .pin3(CLK_out), .pin4(n7474_1_pin10), .pin5(n7474_2_pin5),
    .pin7(n7474_1_pin7), .pin14(n7474_1_pin14), .pin13(CLEAR), .pin12(n7474_2_pin5), .pin11(CLK_out),
    .pin10(n7474_1_pin10), .pin9(n7474_2_pin9));  // open: pin6, pin8
  // Digital_Oscilloscope Palmografos: pin names not known; wires that end beside it: CLK_out, n7474_1_pin5, n7474_1_pin9, n7474_2_pin5, n7474_2_pin9
  // also tied to GND on the sheet: n7474_1_pin7
  // also tied to VCC on the sheet: n7474_1_pin14
endmodule
