// Logisim project askhsh3.circ as structural Verilog: 1 circuit, main circuit main
module main (
  input  CLEAR
);

  wire n7474_1_pin2, n7474_1_pin3, n7474_1_pin5, n7474_1_pin7, n7474_1_pin9, n7474_1_pin14, n7474_2_pin5;

  _7474 #(.ShowInternalStructure("true"), .VccGndPorts("true")) u_7474_1 (
    .pin2(n7474_1_pin2), .pin3(n7474_1_pin3), .pin4(CLEAR), .pin5(n7474_1_pin5), .pin7(n7474_1_pin7),
    .pin14(n7474_1_pin14), .pin13(CLEAR), .pin12(n7474_1_pin5), .pin11(n7474_1_pin3), .pin9(n7474_1_pin9));  // open: pin1, pin6, pin10, pin8
  Clock clock_1 (.out(n7474_1_pin3));
  _7474 #(.ShowInternalStructure("true"), .VccGndPorts("true")) u_7474_2 (
    .pin1(CLEAR), .pin2(n7474_1_pin9), .pin3(n7474_1_pin3), .pin5(n7474_2_pin5), .pin7(n7474_1_pin7),
    .pin14(n7474_1_pin14), .pin13(CLEAR), .pin12(n7474_2_pin5), .pin11(n7474_1_pin3), .pin9(n7474_1_pin2));  // open: pin4, pin6, pin10, pin8
  // Digital_Oscilloscope digital_oscilloscope_1: pin names not known; wires that end beside it: n7474_1_pin3, n7474_1_pin5, n7474_1_pin9, n7474_2_pin5, n7474_1_pin2
  // also tied to GND on the sheet: n7474_1_pin7
  // also tied to VCC on the sheet: n7474_1_pin14
endmodule
