// Logisim project askhsh5.circ as structural Verilog: 21 circuits, main circuit main
module main (
  input  clear,
  input  CLK,
  input  S0,
  input  S1,
  input  ShiftRight,
  input  LN3,
  input  LN1,
  input  ShiftLeft,
  input  LN2,
  input  LN0,
  input  e1,
  input  e2,
  output Q1,
  output Q0,
  output Q3,
  output Q2
);

  wire n7474_1_pin5, n7474_1_pin7, n7474_1_pin9, n7474_1_pin14, n7474_2_pin5, n7474_2_pin9;

  _7474 #(.ShowInternalStructure("true"), .VccGndPorts("true")) u_7474_1 (
    .pin1(clear), .pin2(Q3), .pin3(CLK), .pin5(n7474_1_pin5), .pin7(n7474_1_pin7), .pin14(n7474_1_pin14),
    .pin13(clear), .pin12(Q2), .pin11(CLK), .pin9(n7474_1_pin9));  // open: pin4, pin6, pin10, pin8
  L_74153 l_74153_1 (
    .S0(S0), .S1(S1), .OE1(e1), .A1(n7474_1_pin5), .B1(ShiftRight), .C1(n7474_1_pin9), .D1(LN3), .OE2(e2),
    .A2(n7474_1_pin9), .B2(n7474_1_pin5), .C2(n7474_2_pin5), .D2(LN2), .Y1(Q3), .Y2(Q2));
  LED led_1 (.in(n7474_1_pin9));
  LED led_2 (.in(n7474_1_pin5));
  _7474 #(.ShowInternalStructure("true"), .VccGndPorts("true")) u_7474_2 (
    .pin1(clear), .pin2(Q1), .pin3(CLK), .pin5(n7474_2_pin5), .pin7(n7474_1_pin7), .pin14(n7474_1_pin14),
    .pin13(clear), .pin12(Q0), .pin11(CLK), .pin9(n7474_2_pin9));  // open: pin4, pin6, pin10, pin8
  LED led_3 (.in(n7474_2_pin9));
  LED led_4 (.in(n7474_2_pin5));
  L_74153 l_74153_2 (
    .S0(S0), .S1(S1), .OE1(e1), .A1(n7474_2_pin5), .B1(n7474_1_pin9), .C1(n7474_2_pin9), .D1(LN1), .OE2(e2),
    .A2(n7474_2_pin9), .B2(n7474_2_pin5), .C2(ShiftLeft), .D2(LN0), .Y1(Q1), .Y2(Q0));
  // also tied to GND on the sheet: n7474_1_pin7
  // also tied to VCC on the sheet: n7474_1_pin14
endmodule

module L_74LS00 (
  input  A1,
  input  B1,
  input  A2,
  input  B2,
  input  A3,
  input  B3,
  input  A4,
  input  B4,
  output Y1,
  output Y2,
  output Y3,
  output Y4
);

  nand nand_1 (Y1, A1, B1);
  nand nand_2 (Y2, A2, B2);
  nand nand_3 (Y3, A3, B3);
  nand nand_4 (Y4, A4, B4);
endmodule

module L_74LS02 (
  input  A1,
  input  B1,
  input  A2,
  input  B2,
  input  A3,
  input  B3,
  input  A4,
  input  B4,
  output Y1,
  output Y2,
  output Y3,
  output Y4
);

  nor nor_1 (Y1, A1, B1);
  nor nor_2 (Y2, A2, B2);
  nor nor_3 (Y3, A3, B3);
  nor nor_4 (Y4, A4, B4);
endmodule

module L_74LS03 (
  input  A1,
  input  B1,
  input  A2,
  input  B2,
  input  A3,
  input  B3,
  input  A4,
  input  B4,
  output Y1,
  output Y2,
  output Y3,
  output Y4
);

  wire and_1_out, and_2_out, and_3_out, and_4_out;

  and and_1 (and_1_out, A1, B1);
  and and_2 (and_2_out, A2, B2);
  and and_3 (and_3_out, A3, B3);
  and and_4 (and_4_out, A4, B4);
  assign Y1 = and_1_out ? 1'b0 : 1'bz;  // Controlled_Buffer controlled_buffer_1
  assign Y2 = and_2_out ? 1'b0 : 1'bz;  // Controlled_Buffer controlled_buffer_2
  assign Y3 = and_3_out ? 1'b0 : 1'bz;  // Controlled_Buffer controlled_buffer_3
  assign Y4 = and_4_out ? 1'b0 : 1'bz;  // Controlled_Buffer controlled_buffer_4
endmodule

module L_74LS04 (
  input  A1,
  input  A2,
  input  A3,
  input  A4,
  input  A5,
  input  A6,
  output Y1,
  output Y2,
  output Y3,
  output Y4,
  output Y5,
  output Y6
);

  not not_1 (Y1, A1);
  not not_2 (Y2, A2);
  not not_3 (Y3, A3);
  not not_4 (Y4, A4);
  not not_5 (Y5, A5);
  not not_6 (Y6, A6);
endmodule

module L_74LS08 (
  input  A1,
  input  B1,
  input  A2,
  input  B2,
  input  A3,
  input  B3,
  input  A4,
  input  B4,
  output Y1,
  output Y2,
  output Y3,
  output Y4
);

  and and_1 (Y1, A1, B1);
  and and_2 (Y2, A2, B2);
  and and_3 (Y3, A3, B3);
  and and_4 (Y4, A4, B4);
endmodule

module L_74LS10 (
  input  A1,
  input  B1,
  input  C1,
  input  A2,
  input  B2,
  input  C2,
  input  A3,
  input  B3,
  input  C3,
  output Y1,
  output Y2,
  output Y3
);

  nand nand_1 (Y1, A1, B1, C1);
  nand nand_2 (Y2, A2, B2, C2);
  nand nand_3 (Y3, A3, B3, C3);
endmodule

module L_74LS11 (
  input  A1,
  input  B1,
  input  C1,
  input  A2,
  input  B2,
  input  C2,
  input  A3,
  input  B3,
  input  C3,
  output Y1,
  output Y2,
  output Y3
);

  and and_1 (Y1, A1, B1, C1);
  and and_2 (Y2, A2, B2, C2);
  and and_3 (Y3, A3, B3, C3);
endmodule

module L_74LS20 (
  input  A1,
  input  B1,
  input  C1,
  input  D1,
  input  A2,
  input  B2,
  input  C2,
  input  D2,
  output Y1,
  output Y2
);

  nand nand_1 (Y1, A1, B1, C1, D1);
  nand nand_2 (Y2, A2, B2, C2, D2);
endmodule

module L_74LS21 (
  input  A1,
  input  B1,
  input  C1,
  input  D1,
  input  A2,
  input  B2,
  input  C2,
  input  D2,
  output Y1,
  output Y2
);

  and and_1 (Y1, A1, B1, C1, D1);
  and and_2 (Y2, A2, B2, C2, D2);
endmodule

module L_74LS27 (
  input  A1,
  input  B1,
  input  C1,
  input  A2,
  input  B2,
  input  C2,
  input  A3,
  input  B3,
  input  C3,
  output Y1,
  output Y2,
  output Y3
);

  nor nor_1 (Y1, A1, B1, C1);
  nor nor_2 (Y2, A2, B2, C2);
  nor nor_3 (Y3, A3, B3, C3);
endmodule

module L_74LS30 (
  input  A,
  input  B,
  input  C,
  input  D,
  input  E,
  input  F,
  input  G,
  input  H,
  output Y
);

  nand nand_1 (Y, A, B, C, D, E, F, G, H);
endmodule

module L_74LS32 (
  input  A1,
  input  B1,
  input  A2,
  input  B2,
  input  A3,
  input  B3,
  input  A4,
  input  B4,
  output Y1,
  output Y2,
  output Y3,
  output Y4
);

  or or_1 (Y1, A1, B1);
  or or_2 (Y2, A2, B2);
  or or_3 (Y3, A3, B3);
  or or_4 (Y4, A4, B4);
endmodule

module L_74LS86 (
  input  A1,
  input  B1,
  input  A2,
  input  B2,
  input  A3,
  input  B3,
  input  A4,
  input  B4,
  output Y1,
  output Y2,
  output Y3,
  output Y4
);

  xor xor_1 (Y1, A1, B1);
  xor xor_2 (Y2, A2, B2);
  xor xor_3 (Y3, A3, B3);
  xor xor_4 (Y4, A4, B4);
endmodule

module L_7474 (
  input  SET1,
  input  D1,
  input  CLK1,
  input  CLR1,
  input  SET2,
  input  D2,
  input  CLK2,
  input  CLR2,
  output Q1,
  output Q1_N,
  output Q2,
  output Q2_N
);

  wire not_1_out, not_2_out, not_3_out, not_4_out;

  not not_1 (not_1_out, CLR1);
  not not_2 (not_2_out, CLR2);
  not not_3 (not_3_out, SET1);
  D_Flip_Flop d_ff_1 (.D(D1), .clk(CLK1), .Q(Q1), .Qn(Q1_N), .preset(not_3_out), .reset(not_1_out));
  not not_4 (not_4_out, SET2);
  D_Flip_Flop d_ff_2 (.D(D2), .clk(CLK2), .Q(Q2), .Qn(Q2_N), .preset(not_4_out), .reset(not_2_out));
endmodule

module L_74112 (
  input  SET1,
  input  J1,
  input  K1,
  input  CLK1,
  input  CLR1,
  input  SET2,
  input  J2,
  input  K2,
  input  CLK2,
  input  CLR2,
  output Q1,
  output Q1_N,
  output Q2,
  output Q2_N
);

  wire not_1_out, not_2_out, not_3_out, not_4_out;

  not not_1 (not_1_out, CLR1);
  not not_2 (not_2_out, CLR2);
  not not_3 (not_3_out, SET1);
  J_K_Flip_Flop j_k_ff_1 (.J(J1), .K(K1), .clk(CLK1), .Q(Q1), .Qn(Q1_N), .preset(not_3_out), .reset(not_1_out));
  not not_4 (not_4_out, SET2);
  J_K_Flip_Flop j_k_ff_2 (.J(J2), .K(K2), .clk(CLK2), .Q(Q2), .Qn(Q2_N), .preset(not_4_out), .reset(not_2_out));
endmodule

module L_74x139 (
  input  A0,
  input  A1,
  input  OEA,
  input  B0,
  input  B1,
  input  OEB,
  output Y0,
  output Y1,
  output Y2,
  output Y3,
  output Z0,
  output Z1,
  output Z2,
  output Z3
);

  wire and_1_out, and_2_out, and_3_out, and_4_out, and_5_out, and_6_out, and_7_out, and_8_out, not_1_out,
       not_2_out, not_3_out, not_4_out, not_5_out, not_6_out;

  not not_1 (not_1_out, A0);
  not not_2 (not_2_out, A1);
  not not_3 (not_3_out, OEA);
  not not_4 (not_4_out, B0);
  not not_5 (not_5_out, B1);
  not not_6 (not_6_out, OEB);
  and and_1 (and_1_out, not_1_out, not_2_out, not_3_out);
  and and_2 (and_2_out, A0, not_2_out, not_3_out);
  and and_3 (and_3_out, not_1_out, A1, not_3_out);
  and and_4 (and_4_out, A0, A1, not_3_out);
  and and_5 (and_5_out, not_4_out, not_5_out, not_6_out);
  and and_6 (and_6_out, B0, not_5_out, not_6_out);
  and and_7 (and_7_out, not_4_out, B1, not_6_out);
  and and_8 (and_8_out, B0, B1, not_6_out);
  not not_7 (Y0, and_1_out);
  not not_8 (Y1, and_2_out);
  not not_9 (Y2, and_3_out);
  not not_10 (Y3, and_4_out);
  not not_11 (Z0, and_5_out);
  not not_12 (Z1, and_6_out);
  not not_13 (Z2, and_7_out);
  not not_14 (Z3, and_8_out);
endmodule

module L_74153 (
  input  S0,
  input  S1,
  input  OE1,
  input  A1,
  input  B1,
  input  C1,
  input  D1,
  input  OE2,
  input  A2,
  input  B2,
  input  C2,
  input  D2,
  output Y1,
  output Y2
);

  wire and_1_out, and_2_out, and_3_out, and_4_out, and_5_out, and_6_out, and_7_out, and_8_out, not_1_out,
       not_2_out, not_3_out, not_4_out;

  not not_1 (not_1_out, S1);
  not not_2 (not_2_out, OE1);
  not not_3 (not_3_out, OE2);
  not not_4 (not_4_out, S0);
  and and_1 (and_1_out, A1, not_2_out, not_4_out, not_1_out);
  and and_2 (and_2_out, B1, not_2_out, S0, not_1_out);
  and and_3 (and_3_out, C1, not_2_out, not_4_out, S1);
  and and_4 (and_4_out, D1, not_2_out, S0, S1);
  and and_5 (and_5_out, A2, not_3_out, not_4_out, not_1_out);
  and and_6 (and_6_out, B2, not_3_out, S0, not_1_out);
  and and_7 (and_7_out, C2, not_3_out, not_4_out, S1);
  and and_8 (and_8_out, D2, not_3_out, S0, S1);
  or or_1 (Y1, and_1_out, and_2_out, and_3_out, and_4_out);
  or or_2 (Y2, and_5_out, and_6_out, and_7_out, and_8_out);
endmodule

module L_74181 (
  input  S3,
  input  S2,
  input  S1,
  input  S0,
  input  B3,
  input  A3,
  input  B2,
  input  A2,
  input  B1,
  input  A1,
  input  B0,
  input  A0,
  input  M,
  input  Cn,
  output G,
  output Cn4,
  output P,
  output F3,
  output F2,
  output EQ,
  output F1,
  output F0
);

  wire and_1_out, and_2_out, and_3_out, and_4_out, and_5_out, and_6_out, and_7_out, and_8_out, and_9_out,
       and_10_out, and_11_out, and_12_out, and_13_out, and_14_out, and_15_out, and_16_out, and_17_out,
       and_18_out, and_19_out, and_20_out, and_21_out, and_22_out, and_23_out, and_24_out, and_25_out,
       and_26_out, and_27_out, and_28_out, buffer_1_out, buffer_2_out, buffer_3_out, buffer_4_out,
       buffer_5_out, nand_1_out, nand_3_out, nor_1_out, nor_2_out, nor_3_out, nor_4_out, nor_5_out,
       nor_6_out, nor_7_out, nor_8_out, nor_10_out, nor_11_out, nor_12_out, not_1_out, not_2_out, not_3_out,
       not_4_out, not_5_out, xor_1_out, xor_2_out, xor_3_out, xor_4_out;

  not not_1 (not_1_out, B3);
  not not_2 (not_2_out, B2);
  not not_3 (not_3_out, B1);
  not not_4 (not_4_out, B0);
  not not_5 (not_5_out, M);
  and and_1 (and_1_out, B3, S3, A3);
  and and_2 (and_2_out, A3, S2, not_1_out);
  and and_3 (and_3_out, not_1_out, S1);
  and and_4 (and_4_out, S0, B3);
  buf buffer_1 (buffer_1_out, A3);
  and and_5 (and_5_out, B2, S3, A2);
  and and_6 (and_6_out, A2, S2, not_2_out);
  and and_7 (and_7_out, not_2_out, S1);
  and and_8 (and_8_out, S0, B2);
  buf buffer_2 (buffer_2_out, A2);
  and and_9 (and_9_out, B1, S3, A1);
  and and_10 (and_10_out, A1, S2, not_3_out);
  and and_11 (and_11_out, not_3_out, S1);
  and and_12 (and_12_out, S0, B1);
  buf buffer_3 (buffer_3_out, A1);
  and and_13 (and_13_out, B0, S3, A0);
  and and_14 (and_14_out, A0, S2, not_4_out);
  and and_15 (and_15_out, not_4_out, S1);
  and and_16 (and_16_out, S0, B0);
  buf buffer_4 (buffer_4_out, A0);
  nor nor_1 (nor_1_out, and_1_out, and_2_out);
  nor nor_2 (nor_2_out, and_3_out, and_4_out, buffer_1_out);
  nor nor_3 (nor_3_out, and_5_out, and_6_out);
  nor nor_4 (nor_4_out, and_7_out, and_8_out, buffer_2_out);
  nor nor_5 (nor_5_out, and_9_out, and_10_out);
  nor nor_6 (nor_6_out, and_11_out, and_12_out, buffer_3_out);
  nor nor_7 (nor_7_out, and_13_out, and_14_out);
  nor nor_8 (nor_8_out, and_15_out, and_16_out, buffer_4_out);
  xor xor_1 (xor_1_out, nor_1_out, nor_2_out);
  xor xor_2 (xor_2_out, nor_3_out, nor_4_out);
  xor xor_3 (xor_3_out, nor_5_out, nor_6_out);
  xor xor_4 (xor_4_out, nor_7_out, nor_8_out);
  buf buffer_5 (buffer_5_out, nor_2_out);
  and and_17 (and_17_out, nor_1_out, nor_4_out);
  and and_18 (and_18_out, nor_1_out, nor_3_out, nor_6_out);
  and and_19 (and_19_out, nor_1_out, nor_3_out, nor_5_out, nor_8_out);
  nand nand_1 (nand_1_out, nor_1_out, nor_3_out, nor_5_out, nor_7_out, Cn);
  nand nand_2 (P, nor_1_out, nor_3_out, nor_5_out, nor_7_out);
  and and_20 (and_20_out, Cn, nor_7_out, nor_5_out, nor_3_out, not_5_out);
  and and_21 (and_21_out, nor_5_out, nor_3_out, nor_8_out, not_5_out);
  and and_22 (and_22_out, nor_3_out, nor_6_out, not_5_out);
  and and_23 (and_23_out, nor_4_out, not_5_out);
  and and_24 (and_24_out, Cn, nor_7_out, nor_5_out, not_5_out);
  and and_25 (and_25_out, nor_5_out, nor_8_out, not_5_out);
  and and_26 (and_26_out, nor_6_out, not_5_out);
  and and_27 (and_27_out, Cn, nor_7_out, not_5_out);
  and and_28 (and_28_out, nor_8_out, not_5_out);
  nand nand_3 (nand_3_out, Cn, not_5_out);
  nor nor_9 (G, buffer_5_out, and_17_out, and_18_out, and_19_out);
  nor nor_10 (nor_10_out, and_20_out, and_21_out, and_22_out, and_23_out);
  nor nor_11 (nor_11_out, and_24_out, and_25_out, and_26_out);
  nor nor_12 (nor_12_out, and_27_out, and_28_out);
  nand nand_4 (Cn4, G, nand_1_out);
  xor xor_5 (F3, xor_1_out, nor_10_out);
  xor xor_6 (F2, xor_2_out, nor_11_out);
  xor xor_7 (F1, xor_3_out, nor_12_out);
  xor xor_8 (F0, xor_4_out, nand_3_out);
  and and_29 (EQ, F2, F3, F0, F1);
endmodule

module CD4008 (
  input  Cin,
  input  A0,
  input  A1,
  input  A2,
  input  A3,
  input  B0,
  input  B1,
  input  B2,
  input  B3,
  output S0,
  output S1,
  output S2,
  output S3,
  output Cout
);

  wire adder_1_cout, adder_2_cout, adder_3_cout;

  Adder #(.width(1)) adder_1 (.a(A0), .b(B0), .out(S0), .cin(Cin), .cout(adder_1_cout));
  Adder #(.width(1)) adder_2 (.a(A1), .b(B1), .out(S1), .cin(adder_1_cout), .cout(adder_2_cout));
  Adder #(.width(1)) adder_3 (.a(A2), .b(B2), .out(S2), .cin(adder_2_cout), .cout(adder_3_cout));
  Adder #(.width(1)) adder_4 (.a(A3), .b(B3), .out(S3), .cin(adder_3_cout), .cout(Cout));
endmodule

module askhsh5 (
  input  nCLR,
  input  S0,
  input  S1,
  input  [3:0] A,
  input  e1,
  input  e2,
  input  [3:0] B
);

  wire clock_1_out, main_1_q0, main_1_q1, main_1_q2, main_1_q3, main_2_q0, n7474_1_pin10, n74283_1_pin1,
       n74283_1_pin4, n74283_1_pin7;

  Clock clock_1 (.out(clock_1_out));
  main main_1 (
    .clear(nCLR), .CLK(clock_1_out), .S0(S0), .S1(S1), .ShiftRight(n74283_1_pin4), .LN3(A[3]), .LN1(A[1]),
    .LN2(A[2]), .LN0(A[0]), .e1(e1), .e2(e2), .Q1(main_1_q1), .Q0(main_1_q0), .Q3(main_1_q3), .Q2(main_1_q2));  // open: ShiftLeft
  LED Q1 (.in(main_1_q1));
  LED Q3 (.in(main_1_q3));
  main main_2 (
    .clear(nCLR), .CLK(clock_1_out), .S0(S0), .S1(S1), .LN3(B[3]), .LN1(B[1]), .LN2(B[2]), .LN0(B[0]),
    .e1(e1), .e2(e2), .Q0(main_2_q0));  // open: ShiftRight, ShiftLeft, Q1, Q3, Q2
  LED Q2 (.in(main_1_q2));
  LED Q0 (.in(main_1_q0));
  _74283 #(.ShowInternalStructure("true")) u_74283_1 (
    .pin1(n74283_1_pin1), .pin4(n74283_1_pin4), .pin5(main_1_q0), .pin6(main_2_q0), .pin7(n74283_1_pin7));  // open: pin2, pin3, pin15, pin14, pin13, pin12, pin11, pin10, pin9
  _7474 #(.ShowInternalStructure("true")) u_7474_1 (
    .pin13(nCLR), .pin12(n74283_1_pin1), .pin11(clock_1_out), .pin10(n7474_1_pin10), .pin9(n74283_1_pin7));  // open: pin1, pin2, pin3, pin4, pin5, pin6, pin8
  // also tied to VCC on the sheet: n7474_1_pin10
endmodule
