// Logisim project A1_b.circ as structural Verilog: 1 circuit, main circuit main
module main (
  input  Set,
  input  C_E,
  input  Clear
);

  wire clk_out, l_74112_2_p14, n7408_1_pin1, n7408_1_pin2, n7408_1_pin3, n7408_1_pin9, n7408_1_pin11,
       n7408_1_pin12, sevensegdec_1_p3, sevensegdec_1_p4, sevensegdec_1_p5, sevensegdec_1_p6,
       sevensegdec_1_p7, sevensegdec_1_p8, sevensegdec_1_p9;

  Clock clk (.out(clk_out));
  _7408 #(.ShowInternalStructure("true")) u_7408_1 (
    .pin1(n7408_1_pin1), .pin2(n7408_1_pin2), .pin3(n7408_1_pin3), .pin13(C_E), .pin12(n7408_1_pin12),
    .pin11(n7408_1_pin11), .pin10(n7408_1_pin12), .pin9(n7408_1_pin9), .pin8(n7408_1_pin1));  // open: pin4, pin5, pin6
  // L_74112 l_74112_1: pin names not known; wires that end beside it: Set, C_E, C_E, clk_out, Clear, Set, n7408_1_pin11, n7408_1_pin11, clk_out, Clear, n7408_1_pin12, n7408_1_pin9
  // L_74112 l_74112_2: pin names not known; wires that end beside it: Set, n7408_1_pin1, n7408_1_pin1, clk_out, Clear, Set, n7408_1_pin3, n7408_1_pin3, clk_out, Clear, 1'b1, 1'b0, n7408_1_pin2, l_74112_2_p14, n7408_1_pin9, n7408_1_pin12
  // Digital_Oscilloscope #(.nState(20)) Palmografos: pin names not known; wires that end beside it: clk_out, n7408_1_pin12, n7408_1_pin9, n7408_1_pin2, l_74112_2_p14
  // SevenSegDec sevensegdec_1: pin names not known; wires that end beside it: l_74112_2_p14, n7408_1_pin2, sevensegdec_1_p3, sevensegdec_1_p4, sevensegdec_1_p5, sevensegdec_1_p6, sevensegdec_1_p7, sevensegdec_1_p8, sevensegdec_1_p9
  _7_Segment_Display u_7_segment_display_1 (
    .g(sevensegdec_1_p9), .f(sevensegdec_1_p8), .a(sevensegdec_1_p3), .b(sevensegdec_1_p4),
    .e(sevensegdec_1_p7), .d(sevensegdec_1_p6), .c(sevensegdec_1_p5));  // open: dp
endmodule
