// Logisim project Α2.circ as structural Verilog: 1 circuit, main circuit main
module main (
  input  in_1,
  input  in_2,
  input  in_3
);

  wire clock_1_out, l_74112_1_p9, l_74112_1_p10, l_74112_2_p7, l_74112_2_p8, sevensegdec_1_p4,
       sevensegdec_1_p5, sevensegdec_1_p6, sevensegdec_1_p7, sevensegdec_1_p8, sevensegdec_1_p9,
       sevensegdec_1_p10;

  Clock clock_1 (.out(clock_1_out));
  // _74266 #(.ShowInternalStructure("true")) 74266_1: pin names not known; wires that end beside it: 1'b1, 1'b0
  // L_74112 l_74112_1: pin names not known; wires that end beside it: in_1, in_2, in_2, clock_1_out, in_3, in_1, clock_1_out, in_3, l_74112_1_p9, l_74112_1_p10
  // L_74112 l_74112_2: pin names not known; wires that end beside it: in_1, clock_1_out, in_3, in_1, clock_1_out, in_3, l_74112_2_p7, l_74112_2_p8
  // Digital_Oscilloscope #(.nState(20)) Palmografos: pin names not known; wires that end beside it: clock_1_out, l_74112_1_p9, l_74112_1_p10, l_74112_2_p7, l_74112_2_p8
  // SevenSegDec sevensegdec_1: pin names not known; wires that end beside it: l_74112_2_p8, l_74112_2_p7, l_74112_1_p10, sevensegdec_1_p4, sevensegdec_1_p5, sevensegdec_1_p6, sevensegdec_1_p7, sevensegdec_1_p8, sevensegdec_1_p9, sevensegdec_1_p10
  _7_Segment_Display u_7_segment_display_1 (
    .g(sevensegdec_1_p10), .f(sevensegdec_1_p9), .a(sevensegdec_1_p4), .b(sevensegdec_1_p5),
    .e(sevensegdec_1_p8), .d(sevensegdec_1_p7), .c(sevensegdec_1_p6));  // open: dp
endmodule
