// Logisim project KATSAROS_ANDREAS_AM1084522.circ as structural Verilog: 7 circuits, main circuit main
module main (
  input  in_1,
  input  in_2,
  input  in_3,
  input  in_4,
  input  in_5,
  input  in_6
);

  wire clock_1_out, l_74112_1_q1, l_74112_1_q1_n, l_74112_1_q2, l_74112_1_q2_n, l_74112_2_q1, l_74112_2_q1_n,
       n7408_1_pin3, n7408_1_pin6, n7408_1_pin7, n7408_1_pin8, n7408_1_pin11, n7408_1_pin13, n7408_1_pin14,
       n7408_2_pin11, n7432_1_pin3, n7432_1_pin6, n7432_1_pin7, n7432_1_pin8, n7432_1_pin11, n7432_1_pin14,
       n7432_2_pin3, n7432_2_pin11, n7432_3_pin7, n7432_3_pin8, n7432_3_pin14, sevensegdec_1_a,
       sevensegdec_1_b, sevensegdec_1_c, sevensegdec_1_d, sevensegdec_1_e, sevensegdec_1_f, sevensegdec_1_g;

  Clock clock_1 (.out(clock_1_out));
  L_74112 l_74112_1 (
    .SET1(in_1), .J1(n7432_2_pin3), .K1(n7432_2_pin3), .CLK1(clock_1_out), .CLR1(in_2), .SET2(in_3),
    .J2(n7432_2_pin11), .K2(n7432_2_pin11), .CLK2(clock_1_out), .CLR2(in_4), .Q1(l_74112_1_q1),
    .Q1_N(l_74112_1_q1_n), .Q2(l_74112_1_q2), .Q2_N(l_74112_1_q2_n));
  L_74112 l_74112_2 (
    .SET1(in_5), .J1(n7408_1_pin11), .K1(n7408_1_pin11), .CLK1(clock_1_out), .CLR1(in_6), .Q1(l_74112_2_q1),
    .Q1_N(l_74112_2_q1_n));  // open: SET2, J2, K2, CLK2, CLR2, Q2, Q2_N
  _7432 #(.ShowInternalStructure("true"), .VccGndPorts("true")) u_7432_1 (
    .pin1(l_74112_1_q2_n), .pin2(l_74112_1_q1_n), .pin3(n7432_1_pin3), .pin4(l_74112_1_q1),
    .pin5(l_74112_1_q2), .pin6(n7432_1_pin6), .pin7(n7432_1_pin7), .pin14(n7432_1_pin14),
    .pin13(l_74112_2_q1), .pin12(l_74112_1_q1), .pin11(n7432_1_pin11), .pin10(l_74112_1_q2_n),
    .pin9(n7432_1_pin11), .pin8(n7432_1_pin8));
  _7408 #(.ShowInternalStructure("true"), .VccGndPorts("true")) u_7408_1 (
    .pin1(l_74112_2_q1_n), .pin2(n7432_1_pin3), .pin3(n7408_1_pin3), .pin4(l_74112_2_q1),
    .pin5(n7432_1_pin6), .pin6(n7408_1_pin6), .pin7(n7408_1_pin7), .pin14(n7408_1_pin14),
    .pin13(n7408_1_pin13), .pin12(l_74112_1_q2), .pin11(n7408_1_pin11), .pin10(l_74112_2_q1),
    .pin9(l_74112_1_q2), .pin8(n7408_1_pin8));
  _7432 #(.ShowInternalStructure("true"), .VccGndPorts("true")) u_7432_2 (
    .pin1(l_74112_1_q2_n), .pin2(l_74112_2_q1_n), .pin3(n7432_2_pin3), .pin7(n7408_1_pin7),
    .pin14(n7408_1_pin14), .pin13(l_74112_1_q1), .pin12(n7408_1_pin8), .pin11(n7432_2_pin11),
    .pin10(l_74112_1_q1), .pin9(l_74112_2_q1), .pin8(n7408_1_pin13));  // open: pin4, pin5, pin6
  _7408 #(.ShowInternalStructure("true"), .VccGndPorts("true")) u_7408_2 (
    .pin7(n7408_1_pin7), .pin14(n7408_1_pin14), .pin13(l_74112_2_q1_n), .pin12(l_74112_1_q2),
    .pin11(n7408_2_pin11));  // open: pin1, pin2, pin3, pin4, pin5, pin6, pin10, pin9, pin8
  _7432 #(.ShowInternalStructure("true"), .VccGndPorts("true")) u_7432_3 (
    .pin7(n7432_3_pin7), .pin14(n7432_3_pin14), .pin10(l_74112_1_q1), .pin9(n7408_2_pin11),
    .pin8(n7432_3_pin8));  // open: pin1, pin2, pin3, pin4, pin5, pin6, pin13, pin12, pin11
  SevenSegDec sevensegdec_1 (
    .Q3D(n7432_1_pin8), .Q2C(n7408_1_pin3), .Q1B(n7408_1_pin6), .Q0A(n7432_3_pin8), .a(sevensegdec_1_a),
    .b(sevensegdec_1_b), .c(sevensegdec_1_c), .d(sevensegdec_1_d), .e(sevensegdec_1_e), .f(sevensegdec_1_f),
    .g(sevensegdec_1_g));
  _7_Segment_Display u_7_segment_display_1 (
    .g(sevensegdec_1_g), .f(sevensegdec_1_f), .a(sevensegdec_1_a), .b(sevensegdec_1_b), .e(sevensegdec_1_e),
    .d(sevensegdec_1_d), .c(sevensegdec_1_c));  // open: dp
  // Digital_Oscilloscope digital_oscilloscope_1: pin names not known; wires that end beside it: clock_1_out, n7432_1_pin8, n7408_1_pin3, n7408_1_pin6, n7432_3_pin8
  // also tied to GND on the sheet: {n7432_1_pin7, n7408_1_pin7, n7432_3_pin7}
  // also tied to VCC on the sheet: {n7432_1_pin14, n7408_1_pin14, n7432_3_pin14}
endmodule

module L_74112 (
  input  SET1,
  input  J1,
  input  K1,
  input  CLK1,
  input  CLR1,
  input  SET2,
  input  J2,
  input  K2,
  input  CLK2,
  input  CLR2,
  output Q1,
  output Q1_N,
  output Q2,
  output Q2_N
);

  wire not_1_out, not_2_out, not_3_out, not_4_out, not_5_out, not_6_out;

  not not_1 (not_1_out, CLR1);
  not not_2 (not_2_out, CLR2);
  not not_3 (not_3_out, SET1);
  J_K_Flip_Flop j_k_ff_1 (.J(J1), .K(K1), .clk(not_4_out), .Q(Q1), .Qn(Q1_N), .preset(not_3_out), .reset(not_1_out));
  not not_4 (not_4_out, CLK1);
  not not_5 (not_5_out, SET2);
  J_K_Flip_Flop j_k_ff_2 (.J(J2), .K(K2), .clk(not_6_out), .Q(Q2), .Qn(Q2_N), .preset(not_5_out), .reset(not_2_out));
  not not_6 (not_6_out, CLK2);
endmodule

module L_74x139 (
  input  A0,
  input  A1,
  input  OEA,
  input  B0,
  input  B1,
  input  OEB,
  output Y0,
  output Y1,
  output Y2,
  output Y3,
  output Z0,
  output Z1,
  output Z2,
  output Z3
);

  wire and_1_out, and_2_out, and_3_out, and_4_out, and_5_out, and_6_out, and_7_out, and_8_out, not_1_out,
       not_2_out, not_3_out, not_4_out, not_5_out, not_6_out;

  not not_1 (not_1_out, A0);
  not not_2 (not_2_out, A1);
  not not_3 (not_3_out, OEA);
  not not_4 (not_4_out, B0);
  not not_5 (not_5_out, B1);
  not not_6 (not_6_out, OEB);
  and and_1 (and_1_out, not_1_out, not_2_out, not_3_out);
  and and_2 (and_2_out, A0, not_2_out, not_3_out);
  and and_3 (and_3_out, not_1_out, A1, not_3_out);
  and and_4 (and_4_out, A0, A1, not_3_out);
  and and_5 (and_5_out, not_4_out, not_5_out, not_6_out);
  and and_6 (and_6_out, B0, not_5_out, not_6_out);
  and and_7 (and_7_out, not_4_out, B1, not_6_out);
  and and_8 (and_8_out, B0, B1, not_6_out);
  not not_7 (Y0, and_1_out);
  not not_8 (Y1, and_2_out);
  not not_9 (Y2, and_3_out);
  not not_10 (Y3, and_4_out);
  not not_11 (Z0, and_5_out);
  not not_12 (Z1, and_6_out);
  not not_13 (Z2, and_7_out);
  not not_14 (Z3, and_8_out);
endmodule

module L_74153 (
  input  S0,
  input  S1,
  input  oE1,
  input  I0a,
  input  I1a,
  input  I2a,
  input  I3a,
  input  oE2,
  input  I0b,
  input  I1b,
  input  I2b,
  input  I3b,
  output Za,
  output Zb
);

  wire and_1_out, and_2_out, and_3_out, and_4_out, and_5_out, and_6_out, and_7_out, and_8_out, not_1_out,
       not_2_out, not_3_out, not_4_out;

  not not_1 (not_1_out, oE1);
  not not_2 (not_2_out, oE2);
  not not_3 (not_3_out, S1);
  not not_4 (not_4_out, S0);
  and and_1 (and_1_out, I0a, not_1_out, not_4_out, not_3_out);
  and and_2 (and_2_out, I1a, not_1_out, S0, not_3_out);
  and and_3 (and_3_out, I2a, not_1_out, not_4_out, S1);
  and and_4 (and_4_out, I3a, not_1_out, S0, S1);
  and and_5 (and_5_out, I0b, not_2_out, not_4_out, not_3_out);
  and and_6 (and_6_out, I1b, not_2_out, S0, not_3_out);
  and and_7 (and_7_out, I2b, not_2_out, not_4_out, S1);
  and and_8 (and_8_out, I3b, not_2_out, S0, S1);
  or or_1 (Za, and_1_out, and_2_out, and_3_out, and_4_out);
  or or_2 (Zb, and_5_out, and_6_out, and_7_out, and_8_out);
endmodule

module L_74181 (
  input  S3,
  input  S2,
  input  S1,
  input  S0,
  input  B3,
  input  A3,
  input  B2,
  input  A2,
  input  B1,
  input  A1,
  input  B0,
  input  A0,
  input  M,
  input  Cn,
  output G,
  output Cn4,
  output P,
  output F3,
  output F2,
  output EQ,
  output F1,
  output F0
);

  wire and_1_out, and_2_out, and_3_out, and_4_out, and_5_out, and_6_out, and_7_out, and_8_out, and_9_out,
       and_10_out, and_11_out, and_12_out, and_13_out, and_14_out, and_15_out, and_16_out, and_17_out,
       and_18_out, and_19_out, and_20_out, and_21_out, and_22_out, and_23_out, and_24_out, and_25_out,
       and_26_out, and_27_out, and_28_out, buffer_1_out, buffer_2_out, buffer_3_out, buffer_4_out,
       buffer_5_out, nand_1_out, nand_3_out, nor_1_out, nor_2_out, nor_3_out, nor_4_out, nor_5_out,
       nor_6_out, nor_7_out, nor_8_out, nor_10_out, nor_11_out, nor_12_out, not_1_out, not_2_out, not_3_out,
       not_4_out, not_5_out, xor_1_out, xor_2_out, xor_3_out, xor_4_out;

  not not_1 (not_1_out, B3);
  not not_2 (not_2_out, B2);
  not not_3 (not_3_out, B1);
  not not_4 (not_4_out, B0);
  not not_5 (not_5_out, M);
  and and_1 (and_1_out, B3, S3, A3);
  and and_2 (and_2_out, A3, S2, not_1_out);
  and and_3 (and_3_out, not_1_out, S1);
  and and_4 (and_4_out, S0, B3);
  buf buffer_1 (buffer_1_out, A3);
  and and_5 (and_5_out, B2, S3, A2);
  and and_6 (and_6_out, A2, S2, not_2_out);
  and and_7 (and_7_out, not_2_out, S1);
  and and_8 (and_8_out, S0, B2);
  buf buffer_2 (buffer_2_out, A2);
  and and_9 (and_9_out, B1, S3, A1);
  and and_10 (and_10_out, A1, S2, not_3_out);
  and and_11 (and_11_out, not_3_out, S1);
  and and_12 (and_12_out, S0, B1);
  buf buffer_3 (buffer_3_out, A1);
  and and_13 (and_13_out, B0, S3, A0);
  and and_14 (and_14_out, A0, S2, not_4_out);
  and and_15 (and_15_out, not_4_out, S1);
  and and_16 (and_16_out, S0, B0);
  buf buffer_4 (buffer_4_out, A0);
  nor nor_1 (nor_1_out, and_1_out, and_2_out);
  nor nor_2 (nor_2_out, and_3_out, and_4_out, buffer_1_out);
  nor nor_3 (nor_3_out, and_5_out, and_6_out);
  nor nor_4 (nor_4_out, and_7_out, and_8_out, buffer_2_out);
  nor nor_5 (nor_5_out, and_9_out, and_10_out);
  nor nor_6 (nor_6_out, and_11_out, and_12_out, buffer_3_out);
  nor nor_7 (nor_7_out, and_13_out, and_14_out);
  nor nor_8 (nor_8_out, and_15_out, and_16_out, buffer_4_out);
  xor xor_1 (xor_1_out, nor_1_out, nor_2_out);
  xor xor_2 (xor_2_out, nor_3_out, nor_4_out);
  xor xor_3 (xor_3_out, nor_5_out, nor_6_out);
  xor xor_4 (xor_4_out, nor_7_out, nor_8_out);
  buf buffer_5 (buffer_5_out, nor_2_out);
  and and_17 (and_17_out, nor_1_out, nor_4_out);
  and and_18 (and_18_out, nor_1_out, nor_3_out, nor_6_out);
  and and_19 (and_19_out, nor_1_out, nor_3_out, nor_5_out, nor_8_out);
  nand nand_1 (nand_1_out, nor_1_out, nor_3_out, nor_5_out, nor_7_out, Cn);
  nand nand_2 (P, nor_1_out, nor_3_out, nor_5_out, nor_7_out);
  and and_20 (and_20_out, Cn, nor_7_out, nor_5_out, nor_3_out, not_5_out);
  and and_21 (and_21_out, nor_5_out, nor_3_out, nor_8_out, not_5_out);
  and and_22 (and_22_out, nor_3_out, nor_6_out, not_5_out);
  and and_23 (and_23_out, nor_4_out, not_5_out);
  and and_24 (and_24_out, Cn, nor_7_out, nor_5_out, not_5_out);
  and and_25 (and_25_out, nor_5_out, nor_8_out, not_5_out);
  and and_26 (and_26_out, nor_6_out, not_5_out);
  and and_27 (and_27_out, Cn, nor_7_out, not_5_out);
  and and_28 (and_28_out, nor_8_out, not_5_out);
  nand nand_3 (nand_3_out, Cn, not_5_out);
  nor nor_9 (G, buffer_5_out, and_17_out, and_18_out, and_19_out);
  nor nor_10 (nor_10_out, and_20_out, and_21_out, and_22_out, and_23_out);
  nor nor_11 (nor_11_out, and_24_out, and_25_out, and_26_out);
  nor nor_12 (nor_12_out, and_27_out, and_28_out);
  nand nand_4 (Cn4, G, nand_1_out);
  xor xor_5 (F3, xor_1_out, nor_10_out);
  xor xor_6 (F2, xor_2_out, nor_11_out);
  xor xor_7 (F1, xor_3_out, nor_12_out);
  xor xor_8 (F0, xor_4_out, nand_3_out);
  and and_29 (EQ, F2, F3, F0, F1);
endmodule

module CD4008 (
  input  Cin,
  input  A0,
  input  A1,
  input  A2,
  input  A3,
  input  B0,
  input  B1,
  input  B2,
  input  B3,
  output S0,
  output S1,
  output S2,
  output S3,
  output Cout
);

  wire adder_1_cout, adder_2_cout, adder_3_cout;

  Adder #(.width(1)) adder_1 (.a(A0), .b(B0), .out(S0), .cin(Cin), .cout(adder_1_cout));
  Adder #(.width(1)) adder_2 (.a(A1), .b(B1), .out(S1), .cin(adder_1_cout), .cout(adder_2_cout));
  Adder #(.width(1)) adder_3 (.a(A2), .b(B2), .out(S2), .cin(adder_2_cout), .cout(adder_3_cout));
  Adder #(.width(1)) adder_4 (.a(A3), .b(B3), .out(S3), .cin(adder_3_cout), .cout(Cout));
endmodule

module SevenSegDec (
  input  Q3D,
  input  Q2C,
  input  Q1B,
  input  Q0A,
  output a,
  output b,
  output c,
  output d,
  output e,
  output f,
  output g
);

  wire nand_1_out, nand_2_out, nand_3_out, nand_4_out, nand_5_out, nand_6_out, nand_7_out, nand_8_out,
       nand_9_out, nand_10_out, nand_11_out, nand_12_out, nand_13_out, nand_14_out, nand_15_out, nand_16_out,
       nand_17_out, nand_18_out, nand_19_out, nand_20_out, nand_21_out, nand_22_out, nand_23_out,
       nand_24_out, nand_25_out, nand_26_out, nand_27_out, nand_28_out, nand_29_out, nand_30_out,
       nand_31_out, nand_32_out, nand_33_out, nand_34_out, nand_35_out, nand_36_out, nand_37_out,
       nand_38_out, nand_39_out, nand_40_out, nand_41_out, nand_42_out, nand_43_out, nand_44_out,
       nand_45_out, nand_46_out, nand_47_out, nand_48_out, nand_49_out, nand_50_out, nand_51_out,
       nand_52_out, nand_53_out, nand_54_out, nand_55_out, nand_56_out, nand_57_out, nand_58_out,
       nand_59_out, nand_60_out, nand_61_out, nand_62_out, nand_63_out, nand_64_out, nand_65_out,
       nand_66_out, nand_67_out, nand_68_out, nand_69_out, nand_70_out, nand_71_out, nand_72_out,
       nand_73_out, nand_74_out, nand_75_out, nand_76_out, nand_77_out, nand_78_out, nand_79_out,
       nand_80_out, nand_81_out, nand_82_out, nand_83_out, nand_84_out, nand_85_out, nand_86_out,
       nand_87_out, nand_88_out, nand_89_out, nand_90_out, nand_91_out, nand_92_out, nand_93_out,
       nand_94_out, nand_95_out, nand_96_out, nand_97_out, nand_98_out, nand_99_out, nand_100_out,
       nand_101_out, nand_102_out, nand_103_out, nand_104_out, nand_106_out, nand_107_out, nand_108_out,
       nand_109_out, nand_110_out, nand_111_out, nand_112_out, nand_113_out, nand_114_out, nand_115_out,
       nand_116_out, nand_117_out, nand_118_out, nand_119_out, nand_120_out, nand_121_out, nand_122_out,
       nand_123_out, nand_124_out, nand_125_out, nand_126_out, nand_127_out, nand_128_out, nand_129_out,
       nand_130_out, nand_131_out, nand_132_out, nand_133_out, nand_134_out, nand_136_out, nand_137_out,
       nand_138_out, nand_139_out, nand_141_out, nand_142_out, nand_143_out, nand_144_out, nand_145_out,
       nand_146_out, nand_147_out, nand_148_out;

  nand nand_1 (nand_1_out, Q2C, Q2C);
  nand nand_2 (nand_2_out, Q3D, Q3D);
  nand nand_3 (nand_3_out, Q1B, Q1B);
  nand nand_4 (nand_4_out, Q3D, Q3D);
  nand nand_5 (nand_5_out, Q1B, Q1B);
  nand nand_6 (nand_6_out, Q3D, Q3D);
  nand nand_7 (nand_7_out, Q3D, Q3D);
  nand nand_8 (nand_8_out, Q2C, Q2C);
  nand nand_9 (nand_9_out, Q2C, Q2C);
  nand nand_10 (nand_10_out, Q2C, Q2C);
  nand nand_11 (nand_11_out, Q0A, Q0A);
  nand nand_12 (nand_12_out, Q0A, Q0A);
  nand nand_13 (nand_13_out, Q3D, Q3D);
  nand nand_14 (nand_14_out, Q2C, Q2C);
  nand nand_15 (nand_15_out, Q0A, Q0A);
  nand nand_16 (nand_16_out, Q3D, Q3D);
  nand nand_17 (nand_17_out, Q3D, nand_1_out);
  nand nand_18 (nand_18_out, nand_2_out, nand_3_out);
  nand nand_19 (nand_19_out, nand_4_out, nand_5_out);
  nand nand_20 (nand_20_out, nand_6_out, Q0A);
  nand nand_21 (nand_21_out, nand_7_out, nand_8_out);
  nand nand_22 (nand_22_out, nand_9_out, Q1B);
  nand nand_23 (nand_23_out, nand_10_out, nand_11_out);
  nand nand_24 (nand_24_out, Q1B, nand_12_out);
  nand nand_25 (nand_25_out, Q3D, Q1B);
  nand nand_26 (nand_26_out, Q3D, Q2C);
  nand nand_27 (nand_27_out, nand_13_out, Q2C);
  nand nand_28 (nand_28_out, nand_14_out, Q1B);
  nand nand_29 (nand_29_out, Q1B, nand_15_out);
  nand nand_30 (nand_30_out, nand_16_out, Q2C);
  nand nand_31 (nand_31_out, Q2C, Q2C);
  nand nand_32 (nand_32_out, Q0A, Q0A);
  nand nand_33 (nand_33_out, Q3D, Q3D);
  nand nand_34 (nand_34_out, Q3D, Q3D);
  nand nand_35 (nand_35_out, nand_17_out, nand_17_out);
  nand nand_36 (nand_36_out, Q1B, Q1B);
  nand nand_37 (nand_37_out, Q3D, Q3D);
  nand nand_38 (nand_38_out, Q2C, Q2C);
  nand nand_39 (nand_39_out, nand_18_out, nand_18_out);
  nand nand_40 (nand_40_out, Q0A, Q0A);
  nand nand_41 (nand_41_out, Q3D, Q3D);
  nand nand_42 (nand_42_out, Q1B, Q1B);
  nand nand_43 (nand_43_out, nand_19_out, nand_20_out);
  nand nand_44 (nand_44_out, Q1B, Q1B);
  nand nand_45 (nand_45_out, Q3D, Q3D);
  nand nand_46 (nand_46_out, Q2C, Q2C);
  nand nand_47 (nand_47_out, nand_21_out, nand_21_out);
  nand nand_48 (nand_48_out, Q0A, Q0A);
  nand nand_49 (nand_49_out, nand_22_out, nand_22_out);
  nand nand_50 (nand_50_out, Q1B, Q1B);
  nand nand_51 (nand_51_out, Q1B, Q1B);
  nand nand_52 (nand_52_out, nand_23_out, nand_24_out);
  nand nand_53 (nand_53_out, nand_25_out, nand_26_out);
  nand nand_54 (nand_54_out, Q1B, Q1B);
  nand nand_55 (nand_55_out, Q0A, Q0A);
  nand nand_56 (nand_56_out, nand_27_out, nand_27_out);
  nand nand_57 (nand_57_out, Q1B, Q1B);
  nand nand_58 (nand_58_out, nand_28_out, nand_29_out);
  nand nand_59 (nand_59_out, nand_30_out, nand_30_out);
  nand nand_60 (nand_60_out, Q1B, Q1B);
  nand nand_61 (nand_61_out, Q2C, Q2C);
  nand nand_62 (nand_62_out, nand_31_out, nand_32_out);
  nand nand_63 (nand_63_out, nand_33_out, Q1B);
  nand nand_64 (nand_64_out, nand_34_out, Q2C);
  nand nand_65 (nand_65_out, Q2C, Q1B);
  nand nand_66 (nand_66_out, nand_35_out, nand_36_out);
  nand nand_67 (nand_67_out, nand_37_out, nand_38_out);
  nand nand_68 (nand_68_out, nand_39_out, nand_40_out);
  nand nand_69 (nand_69_out, nand_41_out, Q1B);
  nand nand_70 (nand_70_out, Q3D, nand_42_out);
  nand nand_71 (nand_71_out, nand_43_out, nand_43_out);
  nand nand_72 (nand_72_out, nand_44_out, Q0A);
  nand nand_73 (nand_73_out, nand_45_out, Q2C);
  nand nand_74 (nand_74_out, Q3D, nand_46_out);
  nand nand_75 (nand_75_out, nand_47_out, nand_48_out);
  nand nand_76 (nand_76_out, nand_49_out, Q0A);
  nand nand_77 (nand_77_out, Q2C, nand_50_out);
  nand nand_78 (nand_78_out, Q2C, Q1B);
  nand nand_79 (nand_79_out, Q3D, nand_51_out);
  nand nand_80 (nand_80_out, nand_52_out, nand_52_out);
  nand nand_81 (nand_81_out, nand_53_out, nand_53_out);
  nand nand_82 (nand_82_out, nand_54_out, nand_55_out);
  nand nand_83 (nand_83_out, nand_56_out, nand_57_out);
  nand nand_84 (nand_84_out, nand_58_out, nand_58_out);
  nand nand_85 (nand_85_out, nand_59_out, nand_60_out);
  nand nand_86 (nand_86_out, Q3D, nand_61_out);
  nand nand_87 (nand_87_out, Q3D, Q0A);
  nand nand_88 (nand_88_out, nand_62_out, nand_63_out);
  nand nand_89 (nand_89_out, nand_64_out, nand_64_out);
  nand nand_90 (nand_90_out, nand_65_out, nand_66_out);
  nand nand_91 (nand_91_out, Q0A, Q0A);
  nand nand_92 (nand_92_out, nand_67_out, nand_68_out);
  nand nand_93 (nand_93_out, Q2C, Q2C);
  nand nand_94 (nand_94_out, Q0A, Q0A);
  nand nand_95 (nand_95_out, nand_69_out, nand_69_out);
  nand nand_96 (nand_96_out, nand_70_out, nand_70_out);
  nand nand_97 (nand_97_out, nand_71_out, nand_72_out);
  nand nand_98 (nand_98_out, nand_73_out, nand_74_out);
  nand nand_99 (nand_99_out, nand_75_out, nand_76_out);
  nand nand_100 (nand_100_out, nand_77_out, nand_77_out);
  nand nand_101 (nand_101_out, nand_78_out, nand_78_out);
  nand nand_102 (nand_102_out, Q0A, Q0A);
  nand nand_103 (nand_103_out, nand_79_out, nand_79_out);
  nand nand_104 (nand_104_out, Q0A, Q0A);
  nand nand_105 (e, nand_80_out, nand_81_out);
  nand nand_106 (nand_106_out, nand_82_out, nand_83_out);
  nand nand_107 (nand_107_out, Q0A, Q0A);
  nand nand_108 (nand_108_out, Q2C, Q2C);
  nand nand_109 (nand_109_out, nand_84_out, nand_85_out);
  nand nand_110 (nand_110_out, nand_86_out, nand_87_out);
  nand nand_111 (nand_111_out, nand_88_out, nand_88_out);
  nand nand_112 (nand_112_out, nand_89_out, Q0A);
  nand nand_113 (nand_113_out, nand_90_out, nand_90_out);
  nand nand_114 (nand_114_out, Q3D, nand_91_out);
  nand nand_115 (nand_115_out, nand_92_out, nand_92_out);
  nand nand_116 (nand_116_out, nand_93_out, nand_94_out);
  nand nand_117 (nand_117_out, nand_95_out, Q0A);
  nand nand_118 (nand_118_out, nand_96_out, Q0A);
  nand nand_119 (nand_119_out, nand_97_out, nand_97_out);
  nand nand_120 (nand_120_out, nand_98_out, nand_98_out);
  nand nand_121 (nand_121_out, nand_99_out, nand_99_out);
  nand nand_122 (nand_122_out, nand_100_out, Q0A);
  nand nand_123 (nand_123_out, nand_101_out, nand_102_out);
  nand nand_124 (nand_124_out, nand_103_out, nand_104_out);
  nand nand_125 (nand_125_out, nand_106_out, nand_106_out);
  nand nand_126 (nand_126_out, Q2C, nand_107_out);
  nand nand_127 (nand_127_out, Q3D, nand_108_out);
  nand nand_128 (nand_128_out, Q3D, Q1B);
  nand nand_129 (nand_129_out, nand_109_out, nand_109_out);
  nand nand_130 (nand_130_out, nand_110_out, nand_110_out);
  nand nand_131 (nand_131_out, nand_111_out, nand_112_out);
  nand nand_132 (nand_132_out, nand_113_out, nand_114_out);
  nand nand_133 (nand_133_out, nand_115_out, nand_116_out);
  nand nand_134 (nand_134_out, nand_117_out, nand_118_out);
  nand nand_135 (c, nand_119_out, nand_120_out);
  nand nand_136 (nand_136_out, nand_121_out, nand_122_out);
  nand nand_137 (nand_137_out, nand_123_out, nand_124_out);
  nand nand_138 (nand_138_out, nand_125_out, nand_126_out);
  nand nand_139 (nand_139_out, nand_127_out, nand_128_out);
  nand nand_140 (g, nand_129_out, nand_130_out);
  nand nand_141 (nand_141_out, nand_131_out, nand_131_out);
  nand nand_142 (nand_142_out, nand_132_out, nand_132_out);
  nand nand_143 (nand_143_out, nand_133_out, nand_133_out);
  nand nand_144 (nand_144_out, nand_134_out, nand_134_out);
  nand nand_145 (nand_145_out, nand_136_out, nand_136_out);
  nand nand_146 (nand_146_out, nand_137_out, nand_137_out);
  nand nand_147 (nand_147_out, nand_138_out, nand_138_out);
  nand nand_148 (nand_148_out, nand_139_out, nand_139_out);
  nand nand_149 (a, nand_141_out, nand_142_out);
  nand nand_150 (b, nand_143_out, nand_144_out);
  nand nand_151 (d, nand_145_out, nand_146_out);
  nand nand_152 (f, nand_147_out, nand_148_out);
endmodule
